# Fritzing sketch infitex shift and mux circuit (saved by Fritzing 0.9.2b)
breadboards: 1

parts:
  Part1 = Arduino Mega 2560 (Rev3)
  R1 = Resistor [tolerance=±5% resistance=220 package=THT]
  rkmux_headers = female pin header, 7 pins [form="♀ (female)"]
  rkmux_headers2 = female pin header, 7 pins [form="♀ (female)"]
  rkmux_headers3 = female pin header, 7 pins [form="♀ (female)"]
  rkmux_headers4 = female pin header, 7 pins [form="♀ (female)"]
  J1 = female pin header, 5 pins [form="♀ (female)"]

nets:
  N1: Part1.A0, R1.Pin_1, rkmux_headers.pin1, rkmux_headers2.pin1, rkmux_headers3.pin1, rkmux_headers4.pin1
  N2: Part1.D11_PWM, rkmux_headers4.pin2
  N3: Part1.D10_PWM, rkmux_headers3.pin2
  N4: Part1.D9_PWM, rkmux_headers2.pin2
  N5: Part1.D8_PWM, rkmux_headers.pin2
  N6: Part1.5V, rkmux_headers.pin6, rkmux_headers2.pin6, rkmux_headers3.pin6, rkmux_headers4.pin6, J1.pin2
  N7: Part1.GND, R1.Pin_0, rkmux_headers.pin7, rkmux_headers2.pin7, rkmux_headers3.pin7, rkmux_headers4.pin7, J1.pin1
  N8: Part1.D5_PWM, rkmux_headers.pin3, rkmux_headers2.pin3, rkmux_headers3.pin3, rkmux_headers4.pin3
  N9: Part1.D6_PWM, rkmux_headers.pin4, rkmux_headers2.pin4, rkmux_headers3.pin4, rkmux_headers4.pin4
  N10: Part1.D7_PWM, rkmux_headers.pin5, rkmux_headers2.pin5, rkmux_headers3.pin5, rkmux_headers4.pin5
  N11: Part1.D51, J1.pin4
  N12: Part1.D52, J1.pin5
  N13: Part1.D53, J1.pin3

notes:
  SH_CP of shift breakout board
  ST_CP of shift breakout board
  DS of shift breakout board
  GND of shift breakout board
  +5v of shift breakout board
  Ultra shift-o-tron v4 (4x74HC595N)
  mux1 (4051 breakout) - pin8
  INH
  +5v
  GND
  Z
  s0
  s1
  s2
  mux2 (4051 breakout) - pin9
  mux3 (4051 breakout) - pin9
  mux4 (4051 breakout) - pin9
