# Fritzing sketch infitex shift and single 16 way mux (saved by Fritzing 0.9.2b)
breadboards: 1

parts:
  Part1 = Arduino Mega 2560 (Rev3)
  R1 = Resistor [tolerance=±5% resistance=220 package=THT]
  J1 = female pin header, 5 pins [form="♀ (female)"]
  Part2 = Analog Digital MUX Breakout

nets:
  N1: Part1.A0, R1.Pin_1, Part2.SIG
  N2: Part1.D8_PWM, Part2.S3
  5V: Part1.5V, J1.pin2, Part2.VCC
  GND: Part1.GND, R1.Pin_0, J1.pin1, Part2.GND, Part2.EN
  N3: Part1.D5_PWM, Part2.S0
  N4: Part1.D6_PWM, Part2.S1
  N5: Part1.D7_PWM, Part2.S2
  N6: Part1.D51, J1.pin4
  N7: Part1.D52, J1.pin5
  N8: Part1.D53, J1.pin3

notes:
  SH_CP of shift breakout board
  ST_CP of shift breakout board
  DS of shift breakout board
  GND of shift breakout board
  +5v of shift breakout board
  Ultra shift-o-tron v4 (4x74HC595N)
  INH
  +5v
  GND
  Z
  s0
  s1
  s2
